// Logisim project washing_pipeline.circ as structural Verilog: 39 circuits, main circuit main
module main (
  input  [1:0] MODE,
  input  DOOR_CLOSED,
  input  START,
  input  [7:0] TEMP,
  input  [7:0] DRUM_RPM,
  input  [7:0] WATER_LEVEL,
  input  RESET,
  output [7:0] DISPLAY,
  output VALVE,
  output HEATER,
  output MOTOR_EN,
  output MOTOR_DIR,
  output PUMP_OUT,
  output DOOR_LOCK,
  output BUZZER
);

  wire CLK_out;

  Clock CLK (.out(CLK_out));
  PIPELINE_TOP pipeline_top_1 (
    .MODE(MODE), .DOOR_CLOSED(DOOR_CLOSED), .START(START), .TEMP_IN(TEMP), .DRUM_RPM(DRUM_RPM),
    .WATER_LEVEL(WATER_LEVEL), .CLK(CLK_out), .RESET(RESET), .VALVE_IN(VALVE), .DISPLAY(DISPLAY),
    .HEATER(HEATER), .MOTOR_EN(MOTOR_EN), .MOTOR_DIR(MOTOR_DIR), .PUMP_OUT(PUMP_OUT), .DOOR_LOCK(DOOR_LOCK),
    .BUZZER(BUZZER));
endmodule

module MUX2_1 (
  input  I_p0_f5eba413,
  input  Select,
  input  I_p1_5fa8f914,
  output o_p_ff8cf488
);

  wire and_1_out, and_2_out, not_1_out;

  not not_1 (not_1_out, Select);
  and and_1 (and_1_out, I_p0_f5eba413, not_1_out);
  and and_2 (and_2_out, Select, I_p1_5fa8f914);
  or or_1 (o_p_ff8cf488, and_1_out, and_2_out);
endmodule

module MUX2_8 (
  input  Select,
  input  [7:0] A,
  input  [7:0] B,
  output [7:0] Y
);

  MUX2_1 mux2_1_1 (.I_p0_f5eba413(A[0]), .Select(Select), .I_p1_5fa8f914(B[0]), .o_p_ff8cf488(Y[0]));
  MUX2_1 mux2_1_2 (.I_p0_f5eba413(A[1]), .Select(Select), .I_p1_5fa8f914(B[1]), .o_p_ff8cf488(Y[1]));
  MUX2_1 mux2_1_3 (.I_p0_f5eba413(A[2]), .Select(Select), .I_p1_5fa8f914(B[2]), .o_p_ff8cf488(Y[2]));
  MUX2_1 mux2_1_4 (.I_p0_f5eba413(A[3]), .Select(Select), .I_p1_5fa8f914(B[3]), .o_p_ff8cf488(Y[3]));
  MUX2_1 mux2_1_5 (.I_p0_f5eba413(A[4]), .Select(Select), .I_p1_5fa8f914(B[4]), .o_p_ff8cf488(Y[4]));
  MUX2_1 mux2_1_6 (.I_p0_f5eba413(A[5]), .Select(Select), .I_p1_5fa8f914(B[5]), .o_p_ff8cf488(Y[5]));
  MUX2_1 mux2_1_7 (.I_p0_f5eba413(A[6]), .Select(Select), .I_p1_5fa8f914(B[6]), .o_p_ff8cf488(Y[6]));
  MUX2_1 mux2_1_8 (.I_p0_f5eba413(A[7]), .Select(Select), .I_p1_5fa8f914(B[7]), .o_p_ff8cf488(Y[7]));
endmodule

module FULL_ADDER_1 (
  input  A,
  input  B,
  input  Cin,
  output Sum,
  output Cout
);

  wire and_1_out, and_2_out, xor_1_out;

  xor xor_1 (xor_1_out, A, B);
  xor xor_2 (Sum, xor_1_out, Cin);
  and and_1 (and_1_out, xor_1_out, Cin);
  and and_2 (and_2_out, A, B);
  or or_1 (Cout, and_1_out, and_2_out);
endmodule

module ADD8 (
  input  [7:0] A,
  input  Cin,
  input  [7:0] B,
  output [7:0] Sum,
  output Cout
);

  wire full_adder_1_1_cout, full_adder_1_2_cout, full_adder_1_3_cout, full_adder_1_4_cout,
       full_adder_1_5_cout, full_adder_1_6_cout, full_adder_1_7_cout;

  FULL_ADDER_1 full_adder_1_1 (.A(A[0]), .B(B[0]), .Cin(Cin), .Sum(Sum[0]), .Cout(full_adder_1_1_cout));
  FULL_ADDER_1 full_adder_1_2 (.A(A[1]), .B(B[1]), .Cin(full_adder_1_1_cout), .Sum(Sum[1]), .Cout(full_adder_1_2_cout));
  FULL_ADDER_1 full_adder_1_3 (.A(A[2]), .B(B[2]), .Cin(full_adder_1_2_cout), .Sum(Sum[2]), .Cout(full_adder_1_3_cout));
  FULL_ADDER_1 full_adder_1_4 (.A(A[3]), .B(B[3]), .Cin(full_adder_1_3_cout), .Sum(Sum[3]), .Cout(full_adder_1_4_cout));
  FULL_ADDER_1 full_adder_1_5 (.A(A[4]), .B(B[4]), .Cin(full_adder_1_4_cout), .Sum(Sum[4]), .Cout(full_adder_1_5_cout));
  FULL_ADDER_1 full_adder_1_6 (.A(A[5]), .B(B[5]), .Cin(full_adder_1_5_cout), .Sum(Sum[5]), .Cout(full_adder_1_6_cout));
  FULL_ADDER_1 full_adder_1_7 (.A(A[6]), .B(B[6]), .Cin(full_adder_1_6_cout), .Sum(Sum[6]), .Cout(full_adder_1_7_cout));
  FULL_ADDER_1 full_adder_1_8 (.A(A[7]), .B(B[7]), .Cin(full_adder_1_7_cout), .Sum(Sum[7]), .Cout(Cout));
endmodule

module ADD_SUB8 (
  input  [7:0] B,
  input  SUB,
  input  [7:0] A,
  output [7:0] sum,
  output Cout
);

  wire [7:0] xor_8_out;

  xor xor_1 (xor_8_out[7], SUB, B[7]);
  xor xor_2 (xor_8_out[6], SUB, B[6]);
  xor xor_3 (xor_8_out[5], SUB, B[5]);
  xor xor_4 (xor_8_out[4], SUB, B[4]);
  xor xor_5 (xor_8_out[3], SUB, B[3]);
  xor xor_6 (xor_8_out[2], SUB, B[2]);
  xor xor_7 (xor_8_out[1], SUB, B[1]);
  ADD8 add8_1 (.A(A), .B(xor_8_out), .Cin(SUB), .Sum(sum), .Cout(Cout));
  xor xor_8 (xor_8_out[0], SUB, B[0]);
endmodule

module AND8 (
  input  [7:0] A,
  input  [7:0] B,
  output [7:0] o_p_ff8cf488
);

  and and_1 (o_p_ff8cf488[0], B[0], A[0]);
  and and_2 (o_p_ff8cf488[1], B[1], A[1]);
  and and_3 (o_p_ff8cf488[2], B[2], A[2]);
  and and_4 (o_p_ff8cf488[3], B[3], A[3]);
  and and_5 (o_p_ff8cf488[4], B[4], A[4]);
  and and_6 (o_p_ff8cf488[5], B[5], A[5]);
  and and_7 (o_p_ff8cf488[6], B[6], A[6]);
  and and_8 (o_p_ff8cf488[7], B[7], A[7]);
endmodule

module OR8 (
  input  [7:0] A,
  input  [7:0] B,
  output [7:0] o_p_ff8cf488
);

  or or_1 (o_p_ff8cf488[0], B[0], A[0]);
  or or_2 (o_p_ff8cf488[1], B[1], A[1]);
  or or_3 (o_p_ff8cf488[2], B[2], A[2]);
  or or_4 (o_p_ff8cf488[3], B[3], A[3]);
  or or_5 (o_p_ff8cf488[4], B[4], A[4]);
  or or_6 (o_p_ff8cf488[5], B[5], A[5]);
  or or_7 (o_p_ff8cf488[6], B[6], A[6]);
  or or_8 (o_p_ff8cf488[7], B[7], A[7]);
endmodule

module XOR8 (
  input  [7:0] A,
  input  [7:0] B,
  output [7:0] o_p_ff8cf488
);

  xor xor_1 (o_p_ff8cf488[0], B[0], A[0]);
  xor xor_2 (o_p_ff8cf488[1], B[1], A[1]);
  xor xor_3 (o_p_ff8cf488[2], B[2], A[2]);
  xor xor_4 (o_p_ff8cf488[3], B[3], A[3]);
  xor xor_5 (o_p_ff8cf488[4], B[4], A[4]);
  xor xor_6 (o_p_ff8cf488[5], B[5], A[5]);
  xor xor_7 (o_p_ff8cf488[6], B[6], A[6]);
  xor xor_8 (o_p_ff8cf488[7], B[7], A[7]);
endmodule

module SHIFT8 (
  input  [7:0] A,
  input  DIR,
  output [7:0] o_p_8f3d5cee
);

  MUX2_1 mux2_1_1 (.I_p0_f5eba413(1'b0), .Select(DIR), .I_p1_5fa8f914(A[1]), .o_p_ff8cf488(o_p_8f3d5cee[0]));
  MUX2_1 mux2_1_2 (.I_p0_f5eba413(A[0]), .Select(DIR), .I_p1_5fa8f914(A[2]), .o_p_ff8cf488(o_p_8f3d5cee[1]));
  MUX2_1 mux2_1_3 (.I_p0_f5eba413(A[1]), .Select(DIR), .I_p1_5fa8f914(A[3]), .o_p_ff8cf488(o_p_8f3d5cee[2]));
  MUX2_1 mux2_1_4 (.I_p0_f5eba413(A[2]), .Select(DIR), .I_p1_5fa8f914(A[4]), .o_p_ff8cf488(o_p_8f3d5cee[3]));
  MUX2_1 mux2_1_5 (.I_p0_f5eba413(A[3]), .Select(DIR), .I_p1_5fa8f914(A[5]), .o_p_ff8cf488(o_p_8f3d5cee[4]));
  MUX2_1 mux2_1_6 (.I_p0_f5eba413(A[4]), .Select(DIR), .I_p1_5fa8f914(A[6]), .o_p_ff8cf488(o_p_8f3d5cee[5]));
  MUX2_1 mux2_1_7 (.I_p0_f5eba413(A[5]), .Select(DIR), .I_p1_5fa8f914(A[7]), .o_p_ff8cf488(o_p_8f3d5cee[6]));
  MUX2_1 mux2_1_8 (.I_p0_f5eba413(A[6]), .Select(DIR), .I_p1_5fa8f914(1'b0), .o_p_ff8cf488(o_p_8f3d5cee[7]));
endmodule

module ZERO8 (
  input  [7:0] A,
  output o_p_ff8cf488
);

  wire or_1_out, or_2_out, or_3_out, or_4_out, or_5_out, or_6_out, or_7_out;

  or or_1 (or_1_out, A[0], A[1]);
  or or_2 (or_2_out, A[2], A[3]);
  or or_3 (or_3_out, A[4], A[5]);
  or or_4 (or_4_out, A[6], A[7]);
  or or_5 (or_5_out, or_1_out, or_2_out);
  or or_6 (or_6_out, or_3_out, or_4_out);
  or or_7 (or_7_out, or_5_out, or_6_out);
  not not_1 (o_p_ff8cf488, or_7_out);
endmodule

// DECODER
module DECODER3_8 (
  input  I2,
  input  I1,
  input  I0,
  output O0,
  output O1,
  output O2,
  output O3,
  output O4,
  output O5,
  output O6,
  output O7
);

  wire not_1_out, not_2_out, not_3_out;

  not not_1 (not_1_out, I2);
  not not_2 (not_2_out, I1);
  not not_3 (not_3_out, I0);
  and and_1 (O0, not_1_out, not_2_out, not_3_out);
  and and_2 (O1, not_1_out, not_2_out, I0);
  and and_3 (O2, not_1_out, I1, not_3_out);
  and and_4 (O3, not_1_out, I1, I0);
  and and_5 (O4, I2, not_2_out, not_3_out);
  and and_6 (O5, I2, not_2_out, I0);
  and and_7 (O6, I2, I1, not_3_out);
  and and_8 (O7, I2, I1, I0);
endmodule

// MUX 8-1
module MUX8_1_8 (
  input  [7:0] D0,
  input  [7:0] D1,
  input  [7:0] D2,
  input  [7:0] D3,
  input  [7:0] D4,
  input  [7:0] D5,
  input  [7:0] D6,
  input  [7:0] D7,
  input  [2:0] S_2_0_5b19e2a1,
  output [7:0] Y
);

  wire [7:0] mux2_8_1_y, mux2_8_2_y, mux2_8_3_y, mux2_8_4_y, mux2_8_5_y, mux2_8_6_y;

  MUX2_8 mux2_8_1 (.A(D0), .B(D1), .Select(S_2_0_5b19e2a1[0]), .Y(mux2_8_1_y));
  MUX2_8 mux2_8_2 (.A(D2), .B(D3), .Select(S_2_0_5b19e2a1[0]), .Y(mux2_8_2_y));
  MUX2_8 mux2_8_3 (.A(D4), .B(D5), .Select(S_2_0_5b19e2a1[0]), .Y(mux2_8_3_y));
  MUX2_8 mux2_8_4 (.A(D6), .B(D7), .Select(S_2_0_5b19e2a1[0]), .Y(mux2_8_4_y));
  MUX2_8 mux2_8_5 (.A(mux2_8_1_y), .B(mux2_8_2_y), .Select(S_2_0_5b19e2a1[1]), .Y(mux2_8_5_y));
  MUX2_8 mux2_8_6 (.A(mux2_8_3_y), .B(mux2_8_4_y), .Select(S_2_0_5b19e2a1[1]), .Y(mux2_8_6_y));
  MUX2_8 mux2_8_7 (.A(mux2_8_5_y), .B(mux2_8_6_y), .Select(S_2_0_5b19e2a1[2]), .Y(Y));
endmodule

module REG_FILE (
  input  [2:0] RADDR_A,
  input  [2:0] RADDR_B,
  input  [7:0] WDATA,
  input  [2:0] WADDR,
  input  WE,
  input  CLK,
  input  RESET,
  output [7:0] RDATA_a,
  output [7:0] RDATA_B
);

  wire and_1_out, and_2_out, and_3_out, and_4_out, and_5_out, and_6_out, and_7_out, and_8_out, and_9_out,
       and_10_out, decoder3_8_1_o0, decoder3_8_1_o1, decoder3_8_1_o2, decoder3_8_1_o3, decoder3_8_1_o4,
       decoder3_8_1_o5, decoder3_8_1_o6, decoder3_8_1_o7, eq3_1_eq, eq3_2_eq;
  wire [7:0] mux8_1_8_1_y, mux8_1_8_2_y, register_1_q, register_2_q, register_3_q, register_4_q,
       register_5_q, register_6_q, register_7_q, register_8_q;

  DECODER3_8 decoder3_8_1 (
    .I2(WADDR[2]), .I1(WADDR[1]), .I0(WADDR[0]), .O0(decoder3_8_1_o0), .O1(decoder3_8_1_o1),
    .O2(decoder3_8_1_o2), .O3(decoder3_8_1_o3), .O4(decoder3_8_1_o4), .O5(decoder3_8_1_o5),
    .O6(decoder3_8_1_o6), .O7(decoder3_8_1_o7));
  and and_1 (and_1_out, decoder3_8_1_o0, WE);
  and and_2 (and_2_out, decoder3_8_1_o1, WE);
  and and_3 (and_3_out, decoder3_8_1_o2, WE);
  and and_4 (and_4_out, decoder3_8_1_o3, WE);
  and and_5 (and_5_out, decoder3_8_1_o4, WE);
  and and_6 (and_6_out, decoder3_8_1_o5, WE);
  and and_7 (and_7_out, decoder3_8_1_o6, WE);
  and and_8 (and_8_out, decoder3_8_1_o7, WE);
  Register register_1 (.D(WDATA), .en(and_1_out), .clk(CLK), .Q(register_1_q), .clr(RESET));
  Register register_2 (.D(WDATA), .en(and_2_out), .clk(CLK), .Q(register_2_q), .clr(RESET));
  Register register_3 (.D(WDATA), .en(and_3_out), .clk(CLK), .Q(register_3_q), .clr(RESET));
  Register register_4 (.D(WDATA), .en(and_4_out), .clk(CLK), .Q(register_4_q), .clr(RESET));
  Register register_5 (.D(WDATA), .en(and_5_out), .clk(CLK), .Q(register_5_q), .clr(RESET));
  Register register_6 (.D(WDATA), .en(and_6_out), .clk(CLK), .Q(register_6_q), .clr(RESET));
  Register register_7 (.D(WDATA), .en(and_7_out), .clk(CLK), .Q(register_7_q), .clr(RESET));
  Register register_8 (.D(WDATA), .en(and_8_out), .clk(CLK), .Q(register_8_q), .clr(RESET));
  MUX8_1_8 mux8_1_8_1 (
    .D0(register_1_q), .D1(register_2_q), .D2(register_3_q), .D3(register_4_q), .D4(register_5_q),
    .D5(register_6_q), .D6(register_7_q), .D7(register_8_q), .S_2_0_5b19e2a1(RADDR_A), .Y(mux8_1_8_1_y));
  MUX8_1_8 mux8_1_8_2 (
    .D0(register_1_q), .D1(register_2_q), .D2(register_3_q), .D3(register_4_q), .D4(register_5_q),
    .D5(register_6_q), .D6(register_7_q), .D7(register_8_q), .S_2_0_5b19e2a1(RADDR_B), .Y(mux8_1_8_2_y));
  EQ3 eq3_1 (.A(RADDR_A), .B(WADDR), .EQ(eq3_1_eq));
  EQ3 eq3_2 (.A(RADDR_B), .B(WADDR), .EQ(eq3_2_eq));
  and and_9 (and_9_out, eq3_1_eq, WE);
  and and_10 (and_10_out, eq3_2_eq, WE);
  MUX2_8 mux2_8_1 (.A(mux8_1_8_1_y), .B(WDATA), .Select(and_9_out), .Y(RDATA_a));
  MUX2_8 mux2_8_2 (.A(mux8_1_8_2_y), .B(WDATA), .Select(and_10_out), .Y(RDATA_B));
endmodule

// ALU
module ALU8 (
  input  SUB,
  input  [7:0] A,
  input  [7:0] B,
  input  [2:0] OP,
  input  SHIFT_DIR,
  output COUT,
  output [7:0] aluRes,
  output ZERO
);

  wire [7:0] add_sub8_1_sum, and8_1_o_p_ff8cf488, or8_1_o_p_ff8cf488, shift8_1_o_p_8f3d5cee,
       xor8_1_o_p_ff8cf488;

  ADD_SUB8 add_sub8_1 (.SUB(SUB), .B(B), .A(A), .Cout(COUT), .sum(add_sub8_1_sum));
  AND8 and8_1 (.A(A), .B(B), .o_p_ff8cf488(and8_1_o_p_ff8cf488));
  OR8 or8_1 (.A(A), .B(B), .o_p_ff8cf488(or8_1_o_p_ff8cf488));
  XOR8 xor8_1 (.A(A), .B(B), .o_p_ff8cf488(xor8_1_o_p_ff8cf488));
  SHIFT8 shift8_1 (.DIR(SHIFT_DIR), .A(A), .o_p_8f3d5cee(shift8_1_o_p_8f3d5cee));
  MUX8_1_8 mux8_1_8_1 (
    .D0(add_sub8_1_sum), .D1(and8_1_o_p_ff8cf488), .D2(or8_1_o_p_ff8cf488), .D3(xor8_1_o_p_ff8cf488),
    .D4(shift8_1_o_p_8f3d5cee), .D5(A), .D6(B), .D7({8{1'b0}}), .S_2_0_5b19e2a1(OP), .Y(aluRes));
  ZERO8 zero8_1 (.A(aluRes), .o_p_ff8cf488(ZERO));
endmodule

// CMP
module CMP_U_GE8 (
  input  [7:0] A,
  input  [7:0] B,
  output GE
);

  ADD_SUB8 add_sub8_1 (.SUB(1'b1), .B(B), .A(A), .Cout(GE));  // open: sum
endmodule

module PC (
  input  REDIRECT_VALID,
  input  CLK,
  input  RESET,
  input  STALL_IN,
  input  [7:0] REDIRECT_TARGET,
  input  HALT,
  output [7:0] O_P_0d122a74
);

  wire or_1_out;
  wire [7:0] add8_1_sum, mux2_8_1_y, mux2_8_2_y;

  Register register_1 (.D(mux2_8_2_y), .en(1'b1), .clk(CLK), .Q(O_P_0d122a74), .clr(RESET));
  or or_1 (or_1_out, STALL_IN, HALT);
  ADD8 add8_1 (.A(O_P_0d122a74), .B(8'h1), .Cin(1'b0), .Sum(add8_1_sum));  // open: Cout
  MUX2_8 mux2_8_1 (.A(add8_1_sum), .B(O_P_0d122a74), .Select(or_1_out), .Y(mux2_8_1_y));
  MUX2_8 mux2_8_2 (.A(mux2_8_1_y), .B(REDIRECT_TARGET), .Select(REDIRECT_VALID), .Y(mux2_8_2_y));
endmodule

module IF_STAGE (
  input  REDIRECT_VALID,
  input  STALL_IN,
  input  CLK,
  input  RESET,
  input  [7:0] REDIRECT_TARGET,
  input  HALT,
  output [7:0] PC_OUT,
  output [15:0] INSTR
);

  PC pc_1 (
    .REDIRECT_VALID(REDIRECT_VALID), .CLK(CLK), .RESET(RESET), .STALL_IN(STALL_IN),
    .REDIRECT_TARGET(REDIRECT_TARGET), .HALT(HALT), .O_P_0d122a74(PC_OUT));
  ROM #(.dataWidth(16)) rom_1 (.addr(PC_OUT), .data(INSTR));

  // Notes on the sheet:
  //   contents of rom_1 (hex, n*v repeats v):
  //   10f0 1609 6200 2440 52c0 42c0 a202 1602 54c0 a40e 1864 1e05 160c b011 1896 1e08 1610 1af9 1c01 7d40
  //   1af5 1c00 7d40 1af4 1c01 7d40 1af1 6340 d300 a21f b01a 1800 1af4 7940 1afd 7f40 1af7 1c00 7d40 1afe
  //   1203 14f6 1c01 7340 7c80 1aff 6340 a231 b02e 7880 1afe 7940 1afd 7f40 1af7 1c01 7d40 1afe 1203 14f6
  //   1c01 7340 7c80 1aff 6340 a243 b040 7880 1afe 7940 1af8 1c01 7d40 1af1 6340 140a d440 a44f b049 1af8
  //   7940 1afd 7740 1af7 1c00 7d40 1afe 1203 14f6 1c01 7340 7c80 1aff 6340 a260 b05d 7880 1afe 7940 1af9
  //   7940 1afb 1c01 7d40 1afa 7d40 1af7 1c00 7d40 c000
endmodule

module IF_ID (
  input  REDIRECT_VALID,
  input  [15:0] INSTR_IN,
  input  [7:0] PC_IN,
  input  VALID_IN,
  input  EX_HLT_IN,
  input  CLK,
  input  RESET,
  input  STALL_IN,
  output [15:0] INSTR_OUT,
  output [7:0] PC_OUT,
  output VALID_OUT
);

  wire mux2_1_1_o_p_ff8cf488, mux2_1_2_o_p_ff8cf488, mux2_1_3_o_p_ff8cf488;
  wire [7:0] mux2_8_1_y;
  wire [15:0] mux16_2_1_1_y;

  MUX2_1 mux2_1_1 (
    .I_p0_f5eba413(VALID_IN), .Select(STALL_IN), .I_p1_5fa8f914(VALID_OUT),
    .o_p_ff8cf488(mux2_1_1_o_p_ff8cf488));
  MUX2_1 mux2_1_2 (
    .I_p0_f5eba413(mux2_1_1_o_p_ff8cf488), .Select(EX_HLT_IN), .I_p1_5fa8f914(1'b0),
    .o_p_ff8cf488(mux2_1_2_o_p_ff8cf488));
  MUX16_2_1 mux16_2_1_1 (.B(INSTR_OUT), .A(INSTR_IN), .S(STALL_IN), .Y(mux16_2_1_1_y));
  MUX2_1 mux2_1_3 (
    .I_p0_f5eba413(mux2_1_2_o_p_ff8cf488), .Select(REDIRECT_VALID), .I_p1_5fa8f914(1'b0),
    .o_p_ff8cf488(mux2_1_3_o_p_ff8cf488));
  MUX2_8 mux2_8_1 (.A(PC_IN), .B(PC_OUT), .Select(STALL_IN), .Y(mux2_8_1_y));
  Register #(.width(16)) register_1 (.D(mux16_2_1_1_y), .clk(CLK), .Q(INSTR_OUT), .clr(RESET));  // open: en
  Register register_2 (.D(mux2_8_1_y), .clk(CLK), .Q(PC_OUT), .clr(RESET));  // open: en
  Register #(.width(1)) register_3 (.D(mux2_1_3_o_p_ff8cf488), .clk(CLK), .Q(VALID_OUT), .clr(RESET));  // open: en
endmodule

module ID_STAGE (
  input  [7:0] PC_IN,
  input  [15:0] INSTR,
  input  [7:0] EXEC_RESULT_IN,
  input  [7:0] MEM_DATA_IN,
  input  VALID_IN,
  output [7:0] PC_OUT,
  output [7:0] TARGET,
  output [7:0] IMM,
  output [2:0] RD,
  output [2:0] RS,
  output [7:0] SRC_A,
  output [7:0] SRC_B,
  output RW_OUT,
  output VALID_OUT,
  output MR_OUT,
  output MW_OUT,
  output ALU_SRC_IMM_OUT,
  output SUB_OUT,
  output BRANCH_OUT,
  output BNE_OUT,
  output JMP_OUT,
  output HLT_OUT,
  output USE_A_OUT,
  output USE_B_OUT,
  output CMP_OUT,
  output [2:0] ALU_OP_OUT,
  output [1:0] WB_SEL
);

  MUX2_3 mux2_3_1 (.A(INSTR[8:6]), .B(INSTR[11:9]), .Select(BRANCH_OUT), .Y(RS));
  CONTROL_UNIT control_unit_1 (
    .OPCODE(INSTR[15:12]), .REG_WRITE(RW_OUT), .MEM_READ(MR_OUT), .MEM_WRITE(MW_OUT),
    .ALU_SRC_MEM(ALU_SRC_IMM_OUT), .SUB(SUB_OUT), .BRANCH(BRANCH_OUT), .BRANCH_NE(BNE_OUT), .JUMP(JMP_OUT),
    .HALT(HLT_OUT), .USE_A(USE_A_OUT), .USE_B(USE_B_OUT), .CMP_GE(CMP_OUT), .ALU_OP(ALU_OP_OUT),
    .WB_SEL(WB_SEL));

  assign {IMM[7], IMM[5:0]} = {INSTR[7], INSTR[5:0]};
  assign PC_OUT = PC_IN;
  assign RD = INSTR[11:9];
  assign SRC_A = MEM_DATA_IN;
  assign SRC_B = EXEC_RESULT_IN;
  assign TARGET = {INSTR[7], IMM[6], INSTR[5:0]};
  assign VALID_OUT = VALID_IN;
endmodule

module CONTROL_UNIT (
  input  [3:0] OPCODE,
  output REG_WRITE,
  output MEM_READ,
  output MEM_WRITE,
  output ALU_SRC_MEM,
  output SUB,
  output BRANCH,
  output BRANCH_NE,
  output JUMP,
  output HALT,
  output USE_A,
  output USE_B,
  output CMP_GE,
  output [2:0] ALU_OP,
  output [1:0] WB_SEL
);

  wire decoder4_16_1_o1, decoder4_16_1_o2, decoder4_16_1_o3, decoder4_16_1_o4, decoder4_16_1_o8,
       decoder4_16_1_o9, decoder4_16_1_o14, decoder4_16_1_o15, or_8_out;

  DECODER4_16 decoder4_16_1 (
    .A(OPCODE[3]), .B(OPCODE[2]), .C(OPCODE[1]), .D(OPCODE[0]), .O12(HALT), .O13(CMP_GE),
    .O14(decoder4_16_1_o14), .O15(decoder4_16_1_o15), .O1(decoder4_16_1_o1), .O2(decoder4_16_1_o2),
    .O3(decoder4_16_1_o3), .O4(decoder4_16_1_o4), .O5(ALU_OP[0]), .O6(MEM_READ), .O7(MEM_WRITE),
    .O8(decoder4_16_1_o8), .O9(decoder4_16_1_o9), .O10(BRANCH_NE), .O11(JUMP));  // open: O0
  or or_1 (REG_WRITE, decoder4_16_1_o1, decoder4_16_1_o2, decoder4_16_1_o3, decoder4_16_1_o4, ALU_OP[0], MEM_READ, decoder4_16_1_o8, CMP_GE);
  or or_2 (ALU_SRC_MEM, decoder4_16_1_o1, decoder4_16_1_o8);
  or or_3 (SUB, decoder4_16_1_o4, CMP_GE);
  or or_4 (BRANCH, decoder4_16_1_o9, BRANCH_NE);
  or or_5 (USE_A, decoder4_16_1_o3, decoder4_16_1_o4, ALU_OP[0], MEM_WRITE, decoder4_16_1_o8, CMP_GE);
  or or_6 (USE_B, decoder4_16_1_o2, decoder4_16_1_o3, decoder4_16_1_o4, ALU_OP[0], MEM_READ, MEM_WRITE, decoder4_16_1_o9, BRANCH_NE, CMP_GE);
  or or_7 (ALU_OP[2], decoder4_16_1_o1, or_8_out);
  or or_8 (or_8_out, decoder4_16_1_o2, MEM_READ, MEM_WRITE, decoder4_16_1_o9, BRANCH_NE);
  or or_9 (WB_SEL[0], MEM_READ, CMP_GE);
  or or_10 (WB_SEL[1], decoder4_16_1_o1, CMP_GE);

  assign ALU_OP[1] = ALU_OP[2];
endmodule

module DECODER4_16 (
  input  A,
  input  B,
  input  C,
  input  D,
  output O0,
  output O1,
  output O2,
  output O3,
  output O4,
  output O5,
  output O6,
  output O7,
  output O8,
  output O9,
  output O10,
  output O11,
  output O12,
  output O13,
  output O14,
  output O15
);

  wire not_1_out, not_2_out, not_3_out, not_4_out, undriven;

  not not_1 (not_1_out, A);
  not not_2 (not_2_out, B);
  not not_3 (not_3_out, C);
  not not_4 (not_4_out, D);
  and and_1 (O0, not_1_out, not_2_out, not_3_out, not_4_out);
  and and_2 (O1, not_1_out, not_2_out, not_3_out, D);
  and and_3 (O2, not_1_out, not_2_out, C, not_4_out);
  and and_4 (O3, not_1_out, not_2_out, C, D);
  and and_5 (O4, not_1_out, B, not_3_out, not_4_out);
  and and_6 (O5, not_1_out, B, not_3_out, D);
  and and_7 (O6, not_1_out, B, C, not_4_out);
  and and_8 (O7, not_1_out, B, undriven, D);
  and and_9 (O8, A, not_2_out, not_3_out, not_4_out);
  and and_10 (O9, A, not_2_out, not_3_out, D);
  and and_11 (O10, A, not_2_out, C, not_4_out);
  and and_12 (O11, A, not_2_out, C, D);
  and and_13 (O12, A, B, not_3_out, not_4_out);
  and and_14 (O13, A, B, not_3_out, D);
  and and_15 (O14, A, B, C, not_4_out);
  and and_16 (O15, A, B, C, D);
endmodule

module ID_EX (
  input  [7:0] PC_IN,
  input  [7:0] SRC_A_IN,
  input  [7:0] SRC_B_IN,
  input  [7:0] IMM_IN,
  input  [7:0] TARGET_IN,
  input  [2:0] RD_IN,
  input  [2:0] RS_IN,
  input  [2:0] ALU_OP_IN,
  input  [1:0] WB_SEL_IN,
  input  VALID_IN,
  input  RW_IN,
  input  MR_IN,
  input  MW_IN,
  input  ALU_SRC_IMM_IN,
  input  SUB_IN,
  input  BRANCH_IN,
  input  BNE_IN,
  input  JMP_IN,
  input  HLT_IN,
  input  USE_A_IN,
  input  USE_B_IN,
  input  CMP_IN,
  input  REDIRECT_VALID,
  input  STALL_IN,
  input  EX_HLT_IN,
  input  CLK,
  input  RESET,
  output [7:0] PC_OUT,
  output [7:0] SRC_A_OUT,
  output [7:0] SRC_B_OUT,
  output [7:0] IMM_OUT,
  output [7:0] TARGET,
  output [2:0] RD_OUT,
  output [2:0] RS_OUT,
  output [2:0] ALU_OP_OUT,
  output [1:0] WB_SEL_OUT,
  output VALID_OUT,
  output RW_OUT,
  output MR_OUT,
  output MW_OUT,
  output ALU_SRC_IMM_OUT,
  output SUB_OUT,
  output BRANCH_OUT,
  output BNE_OUT,
  output JMP_OUT,
  output HLT_OUT,
  output USE_A_OUT,
  output USE_B_OUT,
  output CMP_OUT
);

  wire mux2_1_1_o_p_ff8cf488, mux2_1_2_o_p_ff8cf488, mux2_1_3_o_p_ff8cf488;

  MUX2_1 mux2_1_1 (
    .I_p0_f5eba413(VALID_IN), .Select(STALL_IN), .I_p1_5fa8f914(1'b0), .o_p_ff8cf488(mux2_1_1_o_p_ff8cf488));
  MUX2_1 mux2_1_2 (
    .I_p0_f5eba413(mux2_1_1_o_p_ff8cf488), .Select(EX_HLT_IN), .I_p1_5fa8f914(1'b0),
    .o_p_ff8cf488(mux2_1_2_o_p_ff8cf488));
  MUX2_1 mux2_1_3 (
    .I_p0_f5eba413(mux2_1_2_o_p_ff8cf488), .Select(REDIRECT_VALID), .I_p1_5fa8f914(1'b0),
    .o_p_ff8cf488(mux2_1_3_o_p_ff8cf488));
  Register register_1 (.D(PC_IN), .clk(CLK), .Q(PC_OUT), .clr(RESET));  // open: en
  Register register_2 (.D(SRC_A_IN), .clk(CLK), .Q(SRC_A_OUT), .clr(RESET));  // open: en
  Register register_3 (.D(SRC_B_IN), .clk(CLK), .Q(SRC_B_OUT), .clr(RESET));  // open: en
  Register register_4 (.D(IMM_IN), .clk(CLK), .Q(IMM_OUT), .clr(RESET));  // open: en
  Register register_5 (.D(TARGET_IN), .clk(CLK), .Q(TARGET), .clr(RESET));  // open: en
  Register #(.width(3)) register_6 (.D(RD_IN), .clk(CLK), .Q(RD_OUT), .clr(RESET));  // open: en
  Register #(.width(3)) register_7 (.D(RS_IN), .clk(CLK), .Q(RS_OUT), .clr(RESET));  // open: en
  Register #(.width(3)) register_8 (.D(ALU_OP_IN), .clk(CLK), .Q(ALU_OP_OUT), .clr(RESET));  // open: en
  Register #(.width(2)) register_9 (.D(WB_SEL_IN), .clk(CLK), .Q(WB_SEL_OUT), .clr(RESET));  // open: en
  Register #(.width(1)) register_10 (.D(mux2_1_3_o_p_ff8cf488), .clk(CLK), .Q(VALID_OUT), .clr(RESET));  // open: en
  Register #(.width(1)) register_11 (.D(RW_IN), .clk(CLK), .Q(RW_OUT), .clr(RESET));  // open: en
  Register #(.width(1)) register_12 (.D(MR_IN), .clk(CLK), .Q(MR_OUT), .clr(RESET));  // open: en
  Register #(.width(1)) register_13 (.D(MW_IN), .clk(CLK), .Q(MW_OUT), .clr(RESET));  // open: en
  Register #(.width(1)) register_14 (.D(ALU_SRC_IMM_IN), .clk(CLK), .Q(ALU_SRC_IMM_OUT), .clr(RESET));  // open: en
  Register #(.width(1)) register_15 (.D(SUB_IN), .clk(CLK), .Q(SUB_OUT), .clr(RESET));  // open: en
  Register #(.width(1)) register_16 (.D(BRANCH_IN), .clk(CLK), .Q(BRANCH_OUT), .clr(RESET));  // open: en
  Register #(.width(1)) register_17 (.D(BNE_IN), .clk(CLK), .Q(BNE_OUT), .clr(RESET));  // open: en
  Register #(.width(1)) register_18 (.D(JMP_IN), .clk(CLK), .Q(JMP_OUT), .clr(RESET));  // open: en
  Register #(.width(1)) register_19 (.D(HLT_IN), .clk(CLK), .Q(HLT_OUT), .clr(RESET));  // open: en
  Register #(.width(1)) register_20 (.D(USE_A_IN), .clk(CLK), .Q(USE_A_OUT), .clr(RESET));  // open: en
  Register #(.width(1)) register_21 (.D(USE_B_IN), .clk(CLK), .Q(USE_B_OUT), .clr(RESET));  // open: en
  Register #(.width(1)) register_22 (.D(CMP_IN), .clk(CLK), .Q(CMP_OUT), .clr(RESET));  // open: en
endmodule

module MUX2_3 (
  input  [2:0] A,
  input  Select,
  input  [2:0] B,
  output [2:0] Y
);

  MUX2_1 mux2_1_1 (.I_p0_f5eba413(A[0]), .Select(Select), .I_p1_5fa8f914(B[0]), .o_p_ff8cf488(Y[0]));
  MUX2_1 mux2_1_2 (.I_p0_f5eba413(A[1]), .Select(Select), .I_p1_5fa8f914(B[1]), .o_p_ff8cf488(Y[1]));
  MUX2_1 mux2_1_3 (.I_p0_f5eba413(A[2]), .Select(Select), .I_p1_5fa8f914(B[2]), .o_p_ff8cf488(Y[2]));
endmodule

module EX_STAGE (
  input  [7:0] PC_IN,
  input  ALU_SRC_IMM_IN,
  input  [7:0] SRC_A_IN,
  input  [7:0] EXMEM_EX_RES,
  input  SUB_IN,
  input  [7:0] MW_WB_VAL,
  input  [7:0] IMM,
  input  SHIFT_DIR,
  input  CMP_IN,
  input  [7:0] SRC_B_IN,
  input  [2:0] ALU_OP_IN,
  input  [7:0] TARGET_IN,
  input  [2:0] RD_IN,
  input  BNE_IN,
  input  [2:0] EXMEM_RD,
  input  BRANCH_IN,
  input  [2:0] MW_RD,
  input  [2:0] RS_IN,
  input  JMP_IN,
  input  HLT_IN,
  input  EXMEM_REG_WRITE,
  input  EXMEM_MEM_READ,
  input  EXMEM_VALID,
  input  USE_A_IN,
  input  VALID_IN,
  input  USE_B_IN,
  input  MEMWB_VALID,
  input  MEMWB_REG_WRITE,
  input  RW_IN,
  input  MR_IN,
  input  [1:0] WB_SEL_IN,
  input  MW_IN,
  output [7:0] PC_OUT,
  output [7:0] STORE_DATA_OUT,
  output [7:0] ALU_RES_OUT,
  output [7:0] EXEC_RES_OUT,
  output [7:0] REDIRECT_TARGET,
  output [2:0] RD_OUT,
  output REDIRECT_VALID,
  output HALT_OUT,
  output VALID_OUT,
  output RW_OUT,
  output MR_OUT,
  output [1:0] WB_SEL_OUT,
  output MW_OUT
);

  wire alu8_1_cout, alu8_1_zero, and_2_out, and_3_out, and_4_out, and_5_out, and_6_out, and_7_out, eq3_1_eq,
       eq3_2_eq, eq3_3_eq, eq3_4_eq, mux2_1_1_o_p_ff8cf488, not_1_out, zero8_1_o_p_ff8cf488;
  wire [0:0] cmp_u_ge8_1_ge;
  wire [7:0] mux2_8_1_y, mux2_8_2_y, mux2_8_4_y, mux2_8_5_y;

  and and_1 (HALT_OUT, HLT_IN, VALID_IN);
  MUX2_8 mux2_8_1 (.A(SRC_A_IN), .B(MW_WB_VAL), .Select(and_4_out), .Y(mux2_8_1_y));
  MUX2_8 mux2_8_2 (.A(SRC_B_IN), .B(MW_WB_VAL), .Select(and_5_out), .Y(mux2_8_2_y));
  EQ3 eq3_1 (.A(RD_IN), .B(EXMEM_RD), .EQ(eq3_1_eq));
  EQ3 eq3_2 (.A(RD_IN), .B(MW_RD), .EQ(eq3_2_eq));
  EQ3 eq3_3 (.A(RS_IN), .B(EXMEM_RD), .EQ(eq3_3_eq));
  EQ3 eq3_4 (.A(RS_IN), .B(MW_RD), .EQ(eq3_4_eq));
  MUX2_8 mux2_8_3 (.A(mux2_8_1_y), .B(EXMEM_EX_RES), .Select(and_2_out), .Y(STORE_DATA_OUT));
  MUX2_8 mux2_8_4 (.A(mux2_8_2_y), .B(EXMEM_EX_RES), .Select(and_3_out), .Y(mux2_8_4_y));
  and and_2 (and_2_out, eq3_1_eq, EXMEM_REG_WRITE, ~EXMEM_MEM_READ, EXMEM_VALID, USE_A_IN, VALID_IN);  // AND_Gate
  and and_3 (and_3_out, eq3_3_eq, EXMEM_REG_WRITE, ~EXMEM_MEM_READ, EXMEM_VALID, USE_B_IN, VALID_IN);  // AND_Gate
  and and_4 (and_4_out, VALID_IN, USE_A_IN, MEMWB_VALID, eq3_2_eq, MEMWB_REG_WRITE);
  and and_5 (and_5_out, USE_B_IN, MEMWB_VALID, VALID_IN, MEMWB_REG_WRITE, eq3_4_eq);
  MUX2_8 mux2_8_5 (.A(mux2_8_4_y), .B(IMM), .Select(ALU_SRC_IMM_IN), .Y(mux2_8_5_y));
  ZERO8 zero8_1 (.A(mux2_8_4_y), .o_p_ff8cf488(zero8_1_o_p_ff8cf488));
  ALU8 alu8_1 (
    .A(STORE_DATA_OUT), .B(mux2_8_5_y), .SUB(SUB_IN), .SHIFT_DIR(SHIFT_DIR), .OP(ALU_OP_IN),
    .aluRes(ALU_RES_OUT), .COUT(alu8_1_cout), .ZERO(alu8_1_zero));
  CMP_U_GE8 cmp_u_ge8_1 (.A(STORE_DATA_OUT), .B(mux2_8_4_y), .GE(cmp_u_ge8_1_ge[0]));
  not not_1 (not_1_out, zero8_1_o_p_ff8cf488);
  MUX2_8 mux2_8_6 (.A(ALU_RES_OUT), .B({{7{1'b0}}, cmp_u_ge8_1_ge[0]}), .Select(CMP_IN), .Y(EXEC_RES_OUT));
  MUX2_1 mux2_1_1 (
    .I_p0_f5eba413(zero8_1_o_p_ff8cf488), .Select(BNE_IN), .I_p1_5fa8f914(not_1_out),
    .o_p_ff8cf488(mux2_1_1_o_p_ff8cf488));
  and and_6 (and_6_out, mux2_1_1_o_p_ff8cf488, BRANCH_IN, VALID_IN);
  and and_7 (and_7_out, VALID_IN, JMP_IN);
  or or_1 (REDIRECT_VALID, and_7_out, and_6_out);

  assign MR_OUT = MR_IN;
  assign MW_OUT = MW_IN;
  assign PC_OUT = PC_IN;
  assign RD_OUT = RD_IN;
  assign REDIRECT_TARGET = TARGET_IN;
  assign RW_OUT = RW_IN;
  assign VALID_OUT = VALID_IN;
  assign WB_SEL_OUT = WB_SEL_IN;
endmodule

module EQ3 (
  input  [2:0] A,
  input  [2:0] B,
  output EQ
);

  wire xnor_1_out, xnor_2_out, xnor_3_out;

  xnor xnor_1 (xnor_1_out, B[0], A[0]);
  xnor xnor_2 (xnor_2_out, B[1], A[1]);
  xnor xnor_3 (xnor_3_out, B[2], A[2]);
  and and_1 (EQ, xnor_1_out, xnor_2_out, xnor_3_out);
endmodule

module EX_MEM (
  input  [7:0] ALU_RESULT_IN,
  input  [7:0] EXEC_RESULT_IN,
  input  [7:0] STORE_DATA_IN,
  input  [2:0] RD_IN,
  input  [1:0] WB_SEL_IN,
  input  VALID_IN,
  input  REG_WRITE_IN,
  input  MEM_READ_IN,
  input  MEM_WRITE_IN,
  input  CLK,
  input  RESET,
  output [7:0] ALU_RESULT_OUT,
  output [7:0] EXEC_RESULT_OUT,
  output [7:0] STORE_DATA_OUT,
  output [2:0] RD_OUT,
  output [1:0] WB_SEL_OUT,
  output VALID_OUT,
  output REG_WRITE_OUT,
  output MEM_READ_OUT,
  output MEM_WRITE_OUT
);

  Register register_1 (.D(ALU_RESULT_IN), .clk(CLK), .Q(ALU_RESULT_OUT), .clr(RESET));  // open: en
  Register register_2 (.D(EXEC_RESULT_IN), .clk(CLK), .Q(EXEC_RESULT_OUT), .clr(RESET));  // open: en
  Register register_3 (.D(STORE_DATA_IN), .clk(CLK), .Q(STORE_DATA_OUT), .clr(RESET));  // open: en
  Register #(.width(3)) register_4 (.D(RD_IN), .clk(CLK), .Q(RD_OUT), .clr(RESET));  // open: en
  Register #(.width(2)) register_5 (.D(WB_SEL_IN), .clk(CLK), .Q(WB_SEL_OUT), .clr(RESET));  // open: en
  Register #(.width(1)) register_6 (.D(VALID_IN), .clk(CLK), .Q(VALID_OUT), .clr(RESET));  // open: en
  Register #(.width(1)) register_7 (.D(REG_WRITE_IN), .clk(CLK), .Q(REG_WRITE_OUT), .clr(RESET));  // open: en
  Register #(.width(1)) register_8 (.D(MEM_READ_IN), .clk(CLK), .Q(MEM_READ_OUT), .clr(RESET));  // open: en
  Register #(.width(1)) register_9 (.D(MEM_WRITE_IN), .clk(CLK), .Q(MEM_WRITE_OUT), .clr(RESET));  // open: en
endmodule

module MEM_STAGE (
  input  [7:0] ADDR_IN,
  input  [7:0] STORE_DATA_IN,
  input  MEM_READ_IN,
  input  VALID_IN,
  input  MEM_WRITE_IN,
  input  CLK,
  input  START_IN,
  input  RESET,
  input  [1:0] MODE_IN,
  input  [7:0] EXEC_RESULT_IN,
  input  [2:0] RD_IN,
  input  DOOR_CLOSED_IN,
  input  REG_WRITE_IN,
  input  [7:0] WATER_LEVEL_IN,
  input  [1:0] WB_SEL_IN,
  input  [7:0] TEMP_IN,
  input  [7:0] DRUM_RPM_IN,
  output VALVE_IN_OUT,
  output HEATER_OUT,
  output CPU_MOTOR_EN_REQ,
  output MOTOR_DIR_OUT,
  output PUMP_OUT_OUT,
  output DOOR_LOCKED_OUT,
  output BUZZER_OUT,
  output [7:0] DISPLAY_OUT,
  output [7:0] MEM_DATA_OUT,
  output VALID_OUT,
  output [7:0] EXEC_RESULT_OUT,
  output [2:0] RD_OUT,
  output REG_WRITE_OUT,
  output [1:0] WB_SEL_OUT
);

  wire and_1_out, and_2_out, and_3_out, and_4_out, and_5_out, and_6_out, and_7_out, and_8_out, and_9_out,
       and_10_out, and_11_out, and_12_out, and_13_out, and_14_out, and_15_out, and_16_out, and_17_out,
       and_18_out, and_19_out, and_20_out, and_21_out, and_22_out, and_23_out, and_24_out, and_25_out,
       and_26_out, mem_addr_decoder_1_periph_sel, mem_addr_decoder_1_ram_sel, or_1_out,
       periph_addr_decoder_1_sel_buzzer, periph_addr_decoder_1_sel_display,
       periph_addr_decoder_1_sel_door_lock, periph_addr_decoder_1_sel_drum_rpm,
       periph_addr_decoder_1_sel_heater, periph_addr_decoder_1_sel_motor_dir,
       periph_addr_decoder_1_sel_motor_en, periph_addr_decoder_1_sel_pump_out,
       periph_addr_decoder_1_sel_start_mode_door, periph_addr_decoder_1_sel_temp,
       periph_addr_decoder_1_sel_timer_count, periph_addr_decoder_1_sel_timer_ctrl,
       periph_addr_decoder_1_sel_timer_limit, periph_addr_decoder_1_sel_timer_status,
       periph_addr_decoder_1_sel_valve_in, periph_addr_decoder_1_sel_water_level;
  wire [0:0] register_2_q, timer8_1_match_out;
  wire [6:0] mem_addr_decoder_1_addr_out;
  wire [7:0] mux2_8_1_y, mux2_8_2_y, mux2_8_3_y, mux2_8_4_y, mux2_8_5_y, mux2_8_6_y, mux2_8_7_y, mux2_8_8_y,
       mux2_8_9_y, or8_1_o_p_ff8cf488, or8_2_o_p_ff8cf488, or8_4_o_p_ff8cf488, or8_5_o_p_ff8cf488,
       or8_6_o_p_ff8cf488, or8_7_o_p_ff8cf488, or8_8_o_p_ff8cf488, ram_1_dout, register_1_q,
       timer8_1_count_out;

  MEM_ADDR_DECODER mem_addr_decoder_1 (
    .ADDR(ADDR_IN), .ADDR_OUT(mem_addr_decoder_1_addr_out), .RAM_SEL(mem_addr_decoder_1_ram_sel),
    .PERIPH_SEL(mem_addr_decoder_1_periph_sel));  // open: RESERVED_SEL
  and and_1 (and_1_out, MEM_READ_IN, VALID_IN);
  and and_2 (and_2_out, MEM_READ_IN, VALID_IN, mem_addr_decoder_1_ram_sel);
  and and_3 (and_3_out, mem_addr_decoder_1_ram_sel, VALID_IN, MEM_WRITE_IN);
  and and_4 (and_4_out, MEM_WRITE_IN, VALID_IN);
  PERIPH_ADDR_DECODER periph_addr_decoder_1 (
    .ADDRESS(ADDR_IN), .PERIPH_SEL(mem_addr_decoder_1_periph_sel),
    .SEL_START_MODE_DOOR(periph_addr_decoder_1_sel_start_mode_door),
    .SEL_WATER_LEVEL(periph_addr_decoder_1_sel_water_level), .SEL_TEMP(periph_addr_decoder_1_sel_temp),
    .SEL_DRUM_RPM(periph_addr_decoder_1_sel_drum_rpm), .SEL_VALVE_IN(periph_addr_decoder_1_sel_valve_in),
    .SEL_HEATER(periph_addr_decoder_1_sel_heater), .SEL_MOTOR_EN(periph_addr_decoder_1_sel_motor_en),
    .SEL_MOTOR_DIR(periph_addr_decoder_1_sel_motor_dir), .SEL_PUMP_OUT(periph_addr_decoder_1_sel_pump_out),
    .SEL_DOOR_LOCK(periph_addr_decoder_1_sel_door_lock), .SEL_BUZZER(periph_addr_decoder_1_sel_buzzer),
    .SEL_DISPLAY(periph_addr_decoder_1_sel_display), .SEL_TIMER_COUNT(periph_addr_decoder_1_sel_timer_count),
    .SEL_TIMER_LIMIT(periph_addr_decoder_1_sel_timer_limit),
    .SEL_TIMER_CTRL(periph_addr_decoder_1_sel_timer_ctrl),
    .SEL_TIMER_STATUS(periph_addr_decoder_1_sel_timer_status));
  RAM #(.addrWidth(7), .\type ("nonvolatile"), .asyncread("true")) ram_1 (
    .addr(mem_addr_decoder_1_addr_out), .we(and_3_out), .oe(and_2_out), .clk(CLK), .din(STORE_DATA_IN),
    .dout(ram_1_dout));
  and and_5 (and_5_out, mem_addr_decoder_1_periph_sel, and_1_out);
  MUX2_8 mux2_8_1 (.A({8{1'b0}}), .B(ram_1_dout), .Select(and_2_out), .Y(mux2_8_1_y));
  and and_6 (and_6_out, mem_addr_decoder_1_periph_sel, and_4_out);
  or or_1 (or_1_out, and_5_out, and_6_out);
  and and_7 (and_7_out, periph_addr_decoder_1_sel_timer_limit, and_6_out);
  and and_8 (and_8_out, periph_addr_decoder_1_sel_timer_ctrl, and_6_out);
  and and_9 (and_9_out, periph_addr_decoder_1_sel_start_mode_door, and_5_out);
  and and_10 (and_10_out, periph_addr_decoder_1_sel_water_level, and_5_out);
  and and_11 (and_11_out, periph_addr_decoder_1_sel_temp, and_5_out);
  and and_12 (and_12_out, periph_addr_decoder_1_sel_drum_rpm, and_5_out);
  and and_13 (and_13_out, periph_addr_decoder_1_sel_valve_in, and_6_out);
  and and_14 (and_14_out, periph_addr_decoder_1_sel_heater, and_6_out);
  and and_15 (and_15_out, periph_addr_decoder_1_sel_motor_en, and_6_out);
  and and_16 (and_16_out, periph_addr_decoder_1_sel_motor_dir, and_6_out);
  and and_17 (and_17_out, periph_addr_decoder_1_sel_pump_out, and_6_out);
  and and_18 (and_18_out, periph_addr_decoder_1_sel_door_lock, and_6_out);
  and and_19 (and_19_out, periph_addr_decoder_1_sel_buzzer, and_6_out);
  and and_20 (and_20_out, periph_addr_decoder_1_sel_display, and_6_out);
  and and_21 (and_21_out, periph_addr_decoder_1_sel_timer_count, and_5_out);
  and and_22 (and_22_out, periph_addr_decoder_1_sel_timer_limit, and_5_out);
  and and_23 (and_23_out, periph_addr_decoder_1_sel_timer_ctrl, and_5_out);
  // Probe on and_6_out
  and and_24 (and_24_out, periph_addr_decoder_1_sel_timer_status, and_5_out);
  MUX2_8 mux2_8_2 (.A({8{1'b0}}), .B({4'b0000, DOOR_CLOSED_IN, MODE_IN, START_IN}), .Select(and_9_out), .Y(mux2_8_2_y));
  MUX2_8 mux2_8_3 (.A({8{1'b0}}), .B(WATER_LEVEL_IN), .Select(and_10_out), .Y(mux2_8_3_y));
  MUX2_8 mux2_8_4 (.A({8{1'b0}}), .B(TEMP_IN), .Select(and_11_out), .Y(mux2_8_4_y));
  MUX2_8 mux2_8_5 (.A({8{1'b0}}), .B(DRUM_RPM_IN), .Select(and_12_out), .Y(mux2_8_5_y));
  // Probe on and_5_out
  // Probe on or_1_out
  OR8 or8_1 (.A(mux2_8_2_y), .B(mux2_8_3_y), .o_p_ff8cf488(or8_1_o_p_ff8cf488));
  OR8 or8_2 (.A(mux2_8_4_y), .B(mux2_8_5_y), .o_p_ff8cf488(or8_2_o_p_ff8cf488));
  and and_25 (and_25_out, and_8_out, STORE_DATA_IN[2]);
  and and_26 (and_26_out, and_8_out, STORE_DATA_IN[1]);
  OR8 or8_3 (.A(mux2_8_1_y), .B(or8_5_o_p_ff8cf488), .o_p_ff8cf488(MEM_DATA_OUT));
  OR8 or8_4 (.A(or8_1_o_p_ff8cf488), .B(or8_2_o_p_ff8cf488), .o_p_ff8cf488(or8_4_o_p_ff8cf488));
  Register register_1 (.D(STORE_DATA_IN), .en(and_7_out), .clk(CLK), .Q(register_1_q), .clr(RESET));
  Register #(.width(1)) register_2 (.D(STORE_DATA_IN[0]), .en(and_8_out), .clk(CLK), .Q(register_2_q[0]), .clr(RESET));
  Register #(.width(1)) register_3 (.D(STORE_DATA_IN[0]), .en(and_13_out), .clk(CLK), .Q(VALVE_IN_OUT), .clr(RESET));
  Register #(.width(1)) register_4 (.D(STORE_DATA_IN[0]), .en(and_14_out), .clk(CLK), .Q(HEATER_OUT), .clr(RESET));
  Register #(.width(1)) register_5 (
    .D(STORE_DATA_IN[0]), .en(and_15_out), .clk(CLK), .Q(CPU_MOTOR_EN_REQ), .clr(RESET));
  Register #(.width(1)) register_6 (.D(STORE_DATA_IN[0]), .en(and_16_out), .clk(CLK), .Q(MOTOR_DIR_OUT), .clr(RESET));
  Register #(.width(1)) register_7 (.D(STORE_DATA_IN[0]), .en(and_17_out), .clk(CLK), .Q(PUMP_OUT_OUT), .clr(RESET));
  Register #(.width(1)) register_8 (.D(STORE_DATA_IN[0]), .en(and_18_out), .clk(CLK), .Q(DOOR_LOCKED_OUT), .clr(RESET));
  Register #(.width(1)) register_9 (.D(STORE_DATA_IN[0]), .en(and_19_out), .clk(CLK), .Q(BUZZER_OUT), .clr(RESET));
  Register register_10 (.D(STORE_DATA_IN), .en(and_20_out), .clk(CLK), .Q(DISPLAY_OUT), .clr(RESET));
  TIMER8 timer8_1 (
    .LIMIT_IN(register_1_q), .CLEAR_MATCH(and_25_out), .ENABLE(register_2_q[0]), .CLEAR_COUNT(and_26_out),
    .CLK(CLK), .RESET(RESET), .COUNT_OUT(timer8_1_count_out), .MATCH_OUT(timer8_1_match_out[0]));
  MUX2_8 mux2_8_6 (.A({8{1'b0}}), .B(timer8_1_count_out), .Select(and_21_out), .Y(mux2_8_6_y));
  MUX2_8 mux2_8_7 (.A({8{1'b0}}), .B(register_1_q), .Select(and_22_out), .Y(mux2_8_7_y));
  MUX2_8 mux2_8_8 (.A({8{1'b0}}), .B({{7{1'b0}}, register_2_q[0]}), .Select(and_23_out), .Y(mux2_8_8_y));
  MUX2_8 mux2_8_9 (.A({8{1'b0}}), .B({{7{1'b0}}, timer8_1_match_out[0]}), .Select(and_24_out), .Y(mux2_8_9_y));
  OR8 or8_5 (.A(or8_8_o_p_ff8cf488), .B(or8_4_o_p_ff8cf488), .o_p_ff8cf488(or8_5_o_p_ff8cf488));
  OR8 or8_6 (.A(mux2_8_6_y), .B(mux2_8_7_y), .o_p_ff8cf488(or8_6_o_p_ff8cf488));
  OR8 or8_7 (.A(mux2_8_8_y), .B(mux2_8_9_y), .o_p_ff8cf488(or8_7_o_p_ff8cf488));
  OR8 or8_8 (.A(or8_6_o_p_ff8cf488), .B(or8_7_o_p_ff8cf488), .o_p_ff8cf488(or8_8_o_p_ff8cf488));

  assign EXEC_RESULT_OUT = EXEC_RESULT_IN;
  assign RD_OUT = RD_IN;
  assign REG_WRITE_OUT = REG_WRITE_IN;
  assign VALID_OUT = VALID_IN;
  assign WB_SEL_OUT = WB_SEL_IN;
endmodule

module MEM_ADDR_DECODER (
  input  [7:0] ADDR,
  output [6:0] ADDR_OUT,
  output RAM_SEL,
  output RESERVED_SEL,
  output PERIPH_SEL
);

  wire or_1_out;

  not not_1 (RAM_SEL, ADDR[7]);
  and and_1 (PERIPH_SEL, ADDR[4], ADDR[5], ADDR[6], ADDR[7]);
  or or_1 (or_1_out, RAM_SEL, PERIPH_SEL);
  not not_2 (RESERVED_SEL, or_1_out);

  assign ADDR_OUT = ADDR[6:0];
endmodule

module PERIPH_ADDR_DECODER (
  input  [7:0] ADDRESS,
  input  PERIPH_SEL,
  output SEL_START_MODE_DOOR,
  output SEL_WATER_LEVEL,
  output SEL_TEMP,
  output SEL_DRUM_RPM,
  output SEL_VALVE_IN,
  output SEL_HEATER,
  output SEL_MOTOR_EN,
  output SEL_MOTOR_DIR,
  output SEL_PUMP_OUT,
  output SEL_DOOR_LOCK,
  output SEL_BUZZER,
  output SEL_DISPLAY,
  output SEL_TIMER_COUNT,
  output SEL_TIMER_LIMIT,
  output SEL_TIMER_CTRL,
  output SEL_TIMER_STATUS
);

  wire and_1_out, and_2_out, decoder3_8_1_o0, decoder3_8_1_o1, decoder3_8_1_o2, decoder3_8_1_o3,
       decoder3_8_1_o4, decoder3_8_1_o5, decoder3_8_1_o6, decoder3_8_1_o7, not_1_out;

  DECODER3_8 decoder3_8_1 (
    .I2(ADDRESS[2]), .I1(ADDRESS[1]), .I0(ADDRESS[0]), .O0(decoder3_8_1_o0), .O1(decoder3_8_1_o1),
    .O2(decoder3_8_1_o2), .O3(decoder3_8_1_o3), .O4(decoder3_8_1_o4), .O5(decoder3_8_1_o5),
    .O6(decoder3_8_1_o6), .O7(decoder3_8_1_o7));
  not not_1 (not_1_out, ADDRESS[3]);
  and and_1 (and_1_out, not_1_out, PERIPH_SEL);
  and and_2 (and_2_out, ADDRESS[3], PERIPH_SEL);
  and and_3 (SEL_START_MODE_DOOR, decoder3_8_1_o0, and_1_out);
  and and_4 (SEL_WATER_LEVEL, decoder3_8_1_o1, and_1_out);
  and and_5 (SEL_TEMP, decoder3_8_1_o2, and_1_out);
  and and_6 (SEL_DRUM_RPM, decoder3_8_1_o3, and_1_out);
  and and_7 (SEL_VALVE_IN, decoder3_8_1_o4, and_1_out);
  and and_8 (SEL_HEATER, decoder3_8_1_o5, and_1_out);
  and and_9 (SEL_MOTOR_EN, decoder3_8_1_o6, and_1_out);
  and and_10 (SEL_MOTOR_DIR, and_1_out, decoder3_8_1_o7);
  and and_11 (SEL_PUMP_OUT, decoder3_8_1_o0, and_2_out);
  and and_12 (SEL_DOOR_LOCK, decoder3_8_1_o1, and_2_out);
  and and_13 (SEL_BUZZER, decoder3_8_1_o2, and_2_out);
  and and_14 (SEL_DISPLAY, decoder3_8_1_o3, and_2_out);
  and and_15 (SEL_TIMER_COUNT, decoder3_8_1_o4, and_2_out);
  and and_16 (SEL_TIMER_LIMIT, decoder3_8_1_o5, and_2_out);
  and and_17 (SEL_TIMER_CTRL, decoder3_8_1_o6, and_2_out);
  and and_18 (SEL_TIMER_STATUS, decoder3_8_1_o7, and_2_out);
endmodule

module TIMER8 (
  input  [7:0] LIMIT_IN,
  input  ENABLE,
  input  CLEAR_COUNT,
  input  CLEAR_MATCH,
  input  CLK,
  input  RESET,
  output [7:0] COUNT_OUT,
  output MATCH_OUT
);

  wire and_1_out, eq8_1_eq, not_1_out, or_1_out, register_2_q, zero8_1_o_p_ff8cf488;
  wire [7:0] add8_1_sum, mux2_8_1_y, mux2_8_2_y, undriven;

  ADD8 add8_1 (.A(COUNT_OUT), .B(8'h1), .Cin(1'b0), .Sum(add8_1_sum));  // open: Cout
  Register register_1 (.D(mux2_8_2_y), .en(1'b1), .clk(CLK), .Q(COUNT_OUT), .clr(RESET));
  MUX2_8 mux2_8_1 (.A(COUNT_OUT), .B(add8_1_sum), .Select(ENABLE), .Y(mux2_8_1_y));
  Register #(.width(1)) register_2 (.D(MATCH_OUT), .clk(CLK), .Q(register_2_q), .clr(RESET));  // open: en
  MUX2_8 mux2_8_2 (.A(mux2_8_1_y), .B({8{1'b0}}), .Select(CLEAR_COUNT), .Y(mux2_8_2_y));
  EQ8 eq8_1 (.A(undriven), .B(LIMIT_IN), .EQ(eq8_1_eq));
  not not_1 (not_1_out, zero8_1_o_p_ff8cf488);
  ZERO8 zero8_1 (.A(LIMIT_IN), .o_p_ff8cf488(zero8_1_o_p_ff8cf488));
  and and_1 (and_1_out, ENABLE, not_1_out, eq8_1_eq);
  or or_1 (or_1_out, and_1_out, register_2_q);
  MUX2_1 mux2_1_1 (.I_p0_f5eba413(or_1_out), .Select(CLEAR_MATCH), .I_p1_5fa8f914(1'b0), .o_p_ff8cf488(MATCH_OUT));
endmodule

module EQ8 (
  input  [7:0] A,
  input  [7:0] B,
  output EQ
);

  wire eq3_1_eq, eq3_2_eq, xnor_1_out, xnor_2_out;

  EQ3 eq3_1 (.A(A[2:0]), .B(B[2:0]), .EQ(eq3_1_eq));
  xnor xnor_1 (xnor_1_out, A[6], B[6]);
  xnor xnor_2 (xnor_2_out, A[7], B[7]);
  EQ3 eq3_2 (.A(A[5:3]), .B(B[5:3]), .EQ(eq3_2_eq));
  and and_1 (EQ, eq3_1_eq, xnor_1_out, xnor_2_out, eq3_2_eq);
endmodule

module MEM_WB (
  input  [7:0] EXEC_RESULT_IN,
  input  [7:0] MEM_DATA_IN,
  input  [2:0] RD_IN,
  input  VALID_IN,
  input  REG_WRITE_IN,
  input  [1:0] WB_SEL_IN,
  input  CLK,
  input  RESET,
  output [7:0] EXEC_RESULT_OUT,
  output [7:0] MEM_DATA_OUT,
  output [2:0] RD_OUT,
  output VALID_OUT,
  output REG_WRITE_OUT,
  output [1:0] WB_SEL_OUT
);

  Register register_1 (.D(EXEC_RESULT_IN), .clk(CLK), .Q(EXEC_RESULT_OUT), .clr(RESET));  // open: en
  Register register_2 (.D(MEM_DATA_IN), .clk(CLK), .Q(MEM_DATA_OUT), .clr(RESET));  // open: en
  Register #(.width(3)) register_3 (.D(RD_IN), .clk(CLK), .Q(RD_OUT), .clr(RESET));  // open: en
  Register #(.width(1)) register_4 (.D(VALID_IN), .clk(CLK), .Q(VALID_OUT), .clr(RESET));  // open: en
  Register #(.width(1)) register_5 (.D(REG_WRITE_IN), .clk(CLK), .Q(REG_WRITE_OUT), .clr(RESET));  // open: en
  Register #(.width(2)) register_6 (.D(WB_SEL_IN), .clk(CLK), .Q(WB_SEL_OUT));  // open: en, clr
endmodule

module WB_STAGE (
  input  [1:0] WB_SEL_IN,
  input  [7:0] EXEC_RESULT_IN,
  input  [7:0] MEM_DATA_IN,
  input  [2:0] RD_IN,
  input  VALID_IN,
  input  REG_WRITE_IN,
  output [7:0] WB_VALUE_OUT,
  output [2:0] RD_OUT,
  output WB_WRITE_ENABLE
);

  wire [7:0] mux2_8_1_y, mux2_8_2_y;

  and and_1 (WB_WRITE_ENABLE, VALID_IN, REG_WRITE_IN);
  MUX2_8 mux2_8_1 (.A(EXEC_RESULT_IN), .B(MEM_DATA_IN), .Select(WB_SEL_IN[0]), .Y(mux2_8_1_y));
  MUX2_8 mux2_8_2 (.A(EXEC_RESULT_IN), .B(EXEC_RESULT_IN), .Select(WB_SEL_IN[0]), .Y(mux2_8_2_y));
  MUX2_8 mux2_8_3 (.A(mux2_8_1_y), .B(mux2_8_2_y), .Select(WB_SEL_IN[1]), .Y(WB_VALUE_OUT));

  assign RD_OUT = RD_IN;
endmodule

// Washing_Machine
module PIPELINE_TOP (
  input  [1:0] MODE,
  input  DOOR_CLOSED,
  input  START,
  input  [7:0] TEMP_IN,
  input  [7:0] DRUM_RPM,
  input  [7:0] WATER_LEVEL,
  input  CLK,
  input  RESET,
  output VALVE_IN,
  output [7:0] DISPLAY,
  output HEATER,
  output MOTOR_EN,
  output MOTOR_DIR,
  output PUMP_OUT,
  output DOOR_LOCK,
  output BUZZER
);

  wire ex_mem_1_mem_read_out, ex_mem_1_mem_write_out, ex_mem_1_reg_write_out, ex_mem_1_valid_out,
       ex_stage_1_halt_out, ex_stage_1_mr_out, ex_stage_1_mw_out, ex_stage_1_redirect_valid,
       ex_stage_1_rw_out, ex_stage_1_valid_out, id_ex_1_alu_src_imm_out, id_ex_1_bne_out, id_ex_1_branch_out,
       id_ex_1_cmp_out, id_ex_1_hlt_out, id_ex_1_jmp_out, id_ex_1_mr_out, id_ex_1_mw_out, id_ex_1_rw_out,
       id_ex_1_sub_out, id_ex_1_use_a_out, id_ex_1_use_b_out, id_ex_1_valid_out, id_stage_1_alu_src_imm_out,
       id_stage_1_bne_out, id_stage_1_branch_out, id_stage_1_cmp_out, id_stage_1_hlt_out, id_stage_1_jmp_out,
       id_stage_1_mr_out, id_stage_1_mw_out, id_stage_1_rw_out, id_stage_1_sub_out, id_stage_1_use_a_out,
       id_stage_1_use_b_out, id_stage_1_valid_out, if_id_1_valid_out, load_use_hazard_1_stall,
       mem_stage_1_cpu_motor_en_req, mem_stage_1_reg_write_out, mem_stage_1_valid_out,
       mem_wb_1_reg_write_out, mem_wb_1_valid_out, motor_safety_1_trip, Sticky_HALT_halted,
       wb_stage_1_wb_write_enable;
  wire [1:0] ex_mem_1_wb_sel_out, ex_stage_1_wb_sel_out, id_ex_1_wb_sel_out, id_stage_1_wb_sel,
       mem_stage_1_wb_sel_out, mem_wb_1_wb_sel_out;
  wire [2:0] ex_mem_1_rd_out, ex_stage_1_rd_out, id_ex_1_alu_op_out, id_ex_1_rd_out, id_ex_1_rs_out,
       id_stage_1_alu_op_out, id_stage_1_rd, id_stage_1_rs, mem_stage_1_rd_out, mem_wb_1_rd_out,
       wb_stage_1_rd_out;
  wire [7:0] ex_mem_1_alu_result_out, ex_mem_1_exec_result_out, ex_mem_1_store_data_out,
       ex_stage_1_alu_res_out, ex_stage_1_exec_res_out, ex_stage_1_pc_out, ex_stage_1_redirect_target,
       ex_stage_1_store_data_out, id_ex_1_imm_out, id_ex_1_pc_out, id_ex_1_src_a_out, id_ex_1_src_b_out,
       id_ex_1_target, id_stage_1_imm, id_stage_1_pc_out, id_stage_1_src_a, id_stage_1_src_b,
       id_stage_1_target, if_id_1_pc_out, if_stage_1_pc_out, mem_stage_1_exec_result_out,
       mem_stage_1_mem_data_out, mem_wb_1_exec_result_out, mem_wb_1_mem_data_out, reg_file_1_rdata_a,
       reg_file_1_rdata_b, wb_stage_1_wb_value_out;
  wire [15:0] if_id_1_instr_out, if_stage_1_instr;

  IF_STAGE if_stage_1 (
    .REDIRECT_VALID(ex_stage_1_redirect_valid), .STALL_IN(load_use_hazard_1_stall), .CLK(CLK), .RESET(RESET),
    .REDIRECT_TARGET(ex_stage_1_redirect_target), .HALT(Sticky_HALT_halted), .PC_OUT(if_stage_1_pc_out),
    .INSTR(if_stage_1_instr));
  IF_ID if_id_1 (
    .VALID_IN(1'b1), .EX_HLT_IN(Sticky_HALT_halted), .REDIRECT_VALID(ex_stage_1_redirect_valid),
    .INSTR_IN(if_stage_1_instr), .PC_IN(if_stage_1_pc_out), .CLK(CLK), .RESET(RESET),
    .STALL_IN(load_use_hazard_1_stall), .INSTR_OUT(if_id_1_instr_out), .PC_OUT(if_id_1_pc_out),
    .VALID_OUT(if_id_1_valid_out));
  ID_STAGE id_stage_1 (
    .PC_IN(if_id_1_pc_out), .INSTR(if_id_1_instr_out), .EXEC_RESULT_IN(reg_file_1_rdata_b),
    .MEM_DATA_IN(reg_file_1_rdata_a), .VALID_IN(if_id_1_valid_out), .PC_OUT(id_stage_1_pc_out),
    .TARGET(id_stage_1_target), .IMM(id_stage_1_imm), .RD(id_stage_1_rd), .RS(id_stage_1_rs),
    .SRC_A(id_stage_1_src_a), .SRC_B(id_stage_1_src_b), .RW_OUT(id_stage_1_rw_out),
    .VALID_OUT(id_stage_1_valid_out), .MR_OUT(id_stage_1_mr_out), .MW_OUT(id_stage_1_mw_out),
    .ALU_SRC_IMM_OUT(id_stage_1_alu_src_imm_out), .SUB_OUT(id_stage_1_sub_out),
    .BRANCH_OUT(id_stage_1_branch_out), .BNE_OUT(id_stage_1_bne_out), .JMP_OUT(id_stage_1_jmp_out),
    .HLT_OUT(id_stage_1_hlt_out), .USE_A_OUT(id_stage_1_use_a_out), .USE_B_OUT(id_stage_1_use_b_out),
    .CMP_OUT(id_stage_1_cmp_out), .ALU_OP_OUT(id_stage_1_alu_op_out), .WB_SEL(id_stage_1_wb_sel));
  REG_FILE reg_file_1 (
    .WADDR(wb_stage_1_rd_out), .WDATA(wb_stage_1_wb_value_out), .WE(wb_stage_1_wb_write_enable), .CLK(CLK),
    .RESET(RESET), .RADDR_A(id_stage_1_rd), .RADDR_B(id_stage_1_rs), .RDATA_a(reg_file_1_rdata_a),
    .RDATA_B(reg_file_1_rdata_b));
  ID_EX id_ex_1 (
    .MR_IN(id_stage_1_mr_out), .MW_IN(id_stage_1_mw_out), .SUB_IN(id_stage_1_sub_out),
    .CMP_IN(id_stage_1_cmp_out), .RW_IN(id_stage_1_rw_out), .BRANCH_IN(id_stage_1_branch_out),
    .BNE_IN(id_stage_1_bne_out), .JMP_IN(id_stage_1_jmp_out), .HLT_IN(id_stage_1_hlt_out),
    .USE_A_IN(id_stage_1_use_a_out), .USE_B_IN(id_stage_1_use_b_out), .EX_HLT_IN(Sticky_HALT_halted),
    .ALU_SRC_IMM_IN(id_stage_1_alu_src_imm_out), .REDIRECT_VALID(ex_stage_1_redirect_valid),
    .PC_IN(id_stage_1_pc_out), .SRC_A_IN(id_stage_1_src_a), .IMM_IN(id_stage_1_imm),
    .TARGET_IN(id_stage_1_target), .SRC_B_IN(id_stage_1_src_b), .ALU_OP_IN(id_stage_1_alu_op_out),
    .WB_SEL_IN(id_stage_1_wb_sel), .RD_IN(id_stage_1_rd), .RS_IN(id_stage_1_rs), .CLK(CLK), .RESET(RESET),
    .STALL_IN(load_use_hazard_1_stall), .VALID_IN(id_stage_1_valid_out), .MR_OUT(id_ex_1_mr_out),
    .MW_OUT(id_ex_1_mw_out), .ALU_SRC_IMM_OUT(id_ex_1_alu_src_imm_out), .SUB_OUT(id_ex_1_sub_out),
    .SRC_A_OUT(id_ex_1_src_a_out), .BRANCH_OUT(id_ex_1_branch_out), .BNE_OUT(id_ex_1_bne_out),
    .JMP_OUT(id_ex_1_jmp_out), .HLT_OUT(id_ex_1_hlt_out), .USE_A_OUT(id_ex_1_use_a_out),
    .USE_B_OUT(id_ex_1_use_b_out), .SRC_B_OUT(id_ex_1_src_b_out), .TARGET(id_ex_1_target),
    .PC_OUT(id_ex_1_pc_out), .RD_OUT(id_ex_1_rd_out), .RS_OUT(id_ex_1_rs_out),
    .ALU_OP_OUT(id_ex_1_alu_op_out), .WB_SEL_OUT(id_ex_1_wb_sel_out), .RW_OUT(id_ex_1_rw_out),
    .CMP_OUT(id_ex_1_cmp_out), .IMM_OUT(id_ex_1_imm_out), .VALID_OUT(id_ex_1_valid_out));
  LOAD_USE_HAZARD load_use_hazard_1 (
    .ID_SRC_A(id_stage_1_rd), .IDEX_RD(id_ex_1_rd_out), .ID_SRC_B(id_stage_1_rs),
    .ID_VALID(id_stage_1_valid_out), .ID_USE_A(id_stage_1_use_a_out), .IDEX_VALID(id_ex_1_valid_out),
    .ID_USE_B(id_stage_1_use_b_out), .IDEX_MEM_READ(id_ex_1_mr_out), .STALL(load_use_hazard_1_stall));
  // Probe on load_use_hazard_1_stall
  EX_STAGE ex_stage_1 (
    .PC_IN(id_ex_1_pc_out), .ALU_SRC_IMM_IN(id_ex_1_alu_src_imm_out), .SRC_A_IN(id_ex_1_src_a_out),
    .EXMEM_EX_RES(ex_mem_1_exec_result_out), .SUB_IN(id_ex_1_sub_out), .MW_WB_VAL(wb_stage_1_wb_value_out),
    .IMM(id_ex_1_imm_out), .SHIFT_DIR(1'b0), .CMP_IN(id_ex_1_cmp_out), .SRC_B_IN(id_ex_1_src_b_out),
    .ALU_OP_IN(id_ex_1_alu_op_out), .TARGET_IN(id_ex_1_target), .RD_IN(id_ex_1_rd_out),
    .BNE_IN(id_ex_1_bne_out), .EXMEM_RD(ex_mem_1_rd_out), .BRANCH_IN(id_ex_1_branch_out),
    .MW_RD(mem_wb_1_rd_out), .RS_IN(id_ex_1_rs_out), .JMP_IN(id_ex_1_jmp_out), .HLT_IN(id_ex_1_hlt_out),
    .EXMEM_REG_WRITE(ex_mem_1_reg_write_out), .EXMEM_MEM_READ(ex_mem_1_mem_read_out),
    .EXMEM_VALID(ex_mem_1_valid_out), .USE_A_IN(id_ex_1_use_a_out), .VALID_IN(id_ex_1_valid_out),
    .USE_B_IN(id_ex_1_use_b_out), .MEMWB_VALID(mem_wb_1_valid_out), .MEMWB_REG_WRITE(mem_wb_1_reg_write_out),
    .RW_IN(id_ex_1_rw_out), .MR_IN(id_ex_1_mr_out), .WB_SEL_IN(id_ex_1_wb_sel_out), .MW_IN(id_ex_1_mw_out),
    .PC_OUT(ex_stage_1_pc_out), .STORE_DATA_OUT(ex_stage_1_store_data_out),
    .ALU_RES_OUT(ex_stage_1_alu_res_out), .EXEC_RES_OUT(ex_stage_1_exec_res_out),
    .REDIRECT_TARGET(ex_stage_1_redirect_target), .RD_OUT(ex_stage_1_rd_out),
    .REDIRECT_VALID(ex_stage_1_redirect_valid), .HALT_OUT(ex_stage_1_halt_out),
    .VALID_OUT(ex_stage_1_valid_out), .RW_OUT(ex_stage_1_rw_out), .MR_OUT(ex_stage_1_mr_out),
    .WB_SEL_OUT(ex_stage_1_wb_sel_out), .MW_OUT(ex_stage_1_mw_out));
  EX_MEM ex_mem_1 (
    .ALU_RESULT_IN(ex_stage_1_alu_res_out), .EXEC_RESULT_IN(ex_stage_1_exec_res_out),
    .STORE_DATA_IN(ex_stage_1_store_data_out), .RD_IN(ex_stage_1_rd_out), .WB_SEL_IN(ex_stage_1_wb_sel_out),
    .VALID_IN(ex_stage_1_valid_out), .REG_WRITE_IN(ex_stage_1_rw_out), .MEM_READ_IN(ex_stage_1_mr_out),
    .MEM_WRITE_IN(ex_stage_1_mw_out), .CLK(CLK), .RESET(RESET), .ALU_RESULT_OUT(ex_mem_1_alu_result_out),
    .EXEC_RESULT_OUT(ex_mem_1_exec_result_out), .STORE_DATA_OUT(ex_mem_1_store_data_out),
    .RD_OUT(ex_mem_1_rd_out), .WB_SEL_OUT(ex_mem_1_wb_sel_out), .VALID_OUT(ex_mem_1_valid_out),
    .REG_WRITE_OUT(ex_mem_1_reg_write_out), .MEM_READ_OUT(ex_mem_1_mem_read_out),
    .MEM_WRITE_OUT(ex_mem_1_mem_write_out));
  MEM_STAGE mem_stage_1 (
    .RESET(RESET), .MEM_READ_IN(ex_mem_1_mem_read_out), .VALID_IN(ex_mem_1_valid_out),
    .MEM_WRITE_IN(ex_mem_1_mem_write_out), .ADDR_IN(ex_mem_1_alu_result_out),
    .STORE_DATA_IN(ex_mem_1_store_data_out), .REG_WRITE_IN(ex_mem_1_reg_write_out),
    .WB_SEL_IN(ex_mem_1_wb_sel_out), .RD_IN(ex_mem_1_rd_out), .EXEC_RESULT_IN(ex_mem_1_exec_result_out),
    .MODE_IN(MODE), .START_IN(START), .CLK(CLK), .DOOR_CLOSED_IN(DOOR_CLOSED), .WATER_LEVEL_IN(WATER_LEVEL),
    .TEMP_IN(TEMP_IN), .DRUM_RPM_IN(DRUM_RPM), .MEM_DATA_OUT(mem_stage_1_mem_data_out),
    .VALVE_IN_OUT(VALVE_IN), .HEATER_OUT(HEATER), .CPU_MOTOR_EN_REQ(mem_stage_1_cpu_motor_en_req),
    .MOTOR_DIR_OUT(MOTOR_DIR), .PUMP_OUT_OUT(PUMP_OUT), .DOOR_LOCKED_OUT(DOOR_LOCK), .BUZZER_OUT(BUZZER),
    .DISPLAY_OUT(DISPLAY), .VALID_OUT(mem_stage_1_valid_out), .EXEC_RESULT_OUT(mem_stage_1_exec_result_out),
    .RD_OUT(mem_stage_1_rd_out), .REG_WRITE_OUT(mem_stage_1_reg_write_out),
    .WB_SEL_OUT(mem_stage_1_wb_sel_out));
  MEM_WB mem_wb_1 (
    .EXEC_RESULT_IN(mem_stage_1_exec_result_out), .MEM_DATA_IN(mem_stage_1_mem_data_out),
    .RD_IN(mem_stage_1_rd_out), .VALID_IN(mem_stage_1_valid_out), .REG_WRITE_IN(mem_stage_1_reg_write_out),
    .WB_SEL_IN(mem_stage_1_wb_sel_out), .CLK(CLK), .RESET(RESET), .EXEC_RESULT_OUT(mem_wb_1_exec_result_out),
    .MEM_DATA_OUT(mem_wb_1_mem_data_out), .RD_OUT(mem_wb_1_rd_out), .VALID_OUT(mem_wb_1_valid_out),
    .REG_WRITE_OUT(mem_wb_1_reg_write_out), .WB_SEL_OUT(mem_wb_1_wb_sel_out));
  // Probe CPU_MOTOR_REQUEST: pin names not known
  WB_STAGE wb_stage_1 (
    .VALID_IN(mem_wb_1_valid_out), .REG_WRITE_IN(mem_wb_1_reg_write_out), .RD_IN(mem_wb_1_rd_out),
    .EXEC_RESULT_IN(mem_wb_1_exec_result_out), .MEM_DATA_IN(mem_wb_1_mem_data_out),
    .WB_SEL_IN(mem_wb_1_wb_sel_out), .RD_OUT(wb_stage_1_rd_out),
    .WB_WRITE_ENABLE(wb_stage_1_wb_write_enable), .WB_VALUE_OUT(wb_stage_1_wb_value_out));
  MOTOR_SAFETY motor_safety_1 (
    .CPU_MOTOR_EN(mem_stage_1_cpu_motor_en_req), .DOOR_CLOSED(DOOR_CLOSED), .START(START), .CLK(CLK),
    .RESET(RESET), .ACTUAL_MOTOR_EN(MOTOR_EN), .TRIP(motor_safety_1_trip));
  // Probe on motor_safety_1_trip
  HALT_LATCH Sticky_HALT (.EX_HALT(ex_stage_1_halt_out), .CLK(CLK), .RESET(RESET), .HALTED(Sticky_HALT_halted));
endmodule

module LOAD_USE_HAZARD (
  input  [2:0] ID_SRC_A,
  input  [2:0] IDEX_RD,
  input  [2:0] ID_SRC_B,
  input  ID_VALID,
  input  ID_USE_A,
  input  IDEX_VALID,
  input  ID_USE_B,
  input  IDEX_MEM_READ,
  output STALL
);

  wire and_1_out, and_2_out, eq3_1_eq, eq3_2_eq, or_1_out;

  EQ3 eq3_1 (.A(ID_SRC_A), .B(IDEX_RD), .EQ(eq3_1_eq));
  EQ3 eq3_2 (.A(ID_SRC_B), .B(IDEX_RD), .EQ(eq3_2_eq));
  and and_1 (and_1_out, ID_USE_A, eq3_1_eq);
  and and_2 (and_2_out, ID_USE_B, eq3_2_eq);
  or or_1 (or_1_out, and_1_out, and_2_out);
  and and_3 (STALL, ID_VALID, or_1_out, IDEX_VALID, IDEX_MEM_READ);
endmodule

module MOTOR_SAFETY (
  input  CPU_MOTOR_EN,
  input  DOOR_CLOSED,
  input  START,
  input  CLK,
  input  RESET,
  output ACTUAL_MOTOR_EN,
  output TRIP
);

  wire and_1_out, and_2_out, and_4_out, mux2_1_1_o_p_ff8cf488, not_1_out, not_2_out, not_3_out, not_4_out,
       or_1_out, register_2_q;

  and and_1 (and_1_out, CPU_MOTOR_EN, not_1_out);
  not not_1 (not_1_out, DOOR_CLOSED);
  Register #(.width(1)) register_1 (.D(mux2_1_1_o_p_ff8cf488), .en(1'b1), .clk(CLK), .Q(TRIP), .clr(RESET));
  Register #(.width(1)) register_2 (.D(START), .en(1'b1), .clk(CLK), .Q(register_2_q), .clr(RESET));
  or or_1 (or_1_out, and_1_out, TRIP);
  not not_2 (not_2_out, TRIP);
  and and_2 (and_2_out, START, not_3_out);
  not not_3 (not_3_out, register_2_q);
  and and_3 (ACTUAL_MOTOR_EN, CPU_MOTOR_EN, DOOR_CLOSED, not_2_out);
  not not_4 (not_4_out, CPU_MOTOR_EN);
  and and_4 (and_4_out, not_4_out, DOOR_CLOSED, and_2_out);
  MUX2_1 mux2_1_1 (
    .I_p0_f5eba413(or_1_out), .Select(and_4_out), .I_p1_5fa8f914(1'b0), .o_p_ff8cf488(mux2_1_1_o_p_ff8cf488));
endmodule

module MUX16_2_1 (
  input  [15:0] A,
  input  [15:0] B,
  input  S,
  output [15:0] Y
);

  MUX2_1 mux2_1_1 (.I_p0_f5eba413(A[0]), .Select(S), .I_p1_5fa8f914(B[0]), .o_p_ff8cf488(Y[0]));
  MUX2_1 mux2_1_2 (.I_p0_f5eba413(A[1]), .Select(S), .I_p1_5fa8f914(B[1]), .o_p_ff8cf488(Y[1]));
  MUX2_1 mux2_1_3 (.I_p0_f5eba413(A[2]), .Select(S), .I_p1_5fa8f914(B[2]), .o_p_ff8cf488(Y[2]));
  MUX2_1 mux2_1_4 (.I_p0_f5eba413(A[3]), .Select(S), .I_p1_5fa8f914(B[3]), .o_p_ff8cf488(Y[3]));
  MUX2_1 mux2_1_5 (.I_p0_f5eba413(A[4]), .Select(S), .I_p1_5fa8f914(B[4]), .o_p_ff8cf488(Y[4]));
  MUX2_1 mux2_1_6 (.I_p0_f5eba413(A[5]), .Select(S), .I_p1_5fa8f914(B[5]), .o_p_ff8cf488(Y[5]));
  MUX2_1 mux2_1_7 (.I_p0_f5eba413(A[6]), .Select(S), .I_p1_5fa8f914(B[6]), .o_p_ff8cf488(Y[6]));
  MUX2_1 mux2_1_8 (.I_p0_f5eba413(A[7]), .Select(S), .I_p1_5fa8f914(B[7]), .o_p_ff8cf488(Y[7]));
  MUX2_1 mux2_1_9 (.I_p0_f5eba413(A[8]), .Select(S), .I_p1_5fa8f914(B[8]), .o_p_ff8cf488(Y[8]));
  MUX2_1 mux2_1_10 (.I_p0_f5eba413(A[9]), .Select(S), .I_p1_5fa8f914(B[9]), .o_p_ff8cf488(Y[9]));
  MUX2_1 mux2_1_11 (.I_p0_f5eba413(A[10]), .Select(S), .I_p1_5fa8f914(B[10]), .o_p_ff8cf488(Y[10]));
  MUX2_1 mux2_1_12 (.I_p0_f5eba413(A[11]), .Select(S), .I_p1_5fa8f914(B[11]), .o_p_ff8cf488(Y[11]));
  MUX2_1 mux2_1_13 (.I_p0_f5eba413(A[12]), .Select(S), .I_p1_5fa8f914(B[12]), .o_p_ff8cf488(Y[12]));
  MUX2_1 mux2_1_14 (.I_p0_f5eba413(A[13]), .Select(S), .I_p1_5fa8f914(B[13]), .o_p_ff8cf488(Y[13]));
  MUX2_1 mux2_1_15 (.I_p0_f5eba413(A[14]), .Select(S), .I_p1_5fa8f914(B[14]), .o_p_ff8cf488(Y[14]));
  MUX2_1 mux2_1_16 (.I_p0_f5eba413(A[15]), .Select(S), .I_p1_5fa8f914(B[15]), .o_p_ff8cf488(Y[15]));
endmodule

module HALT_LATCH (
  input  EX_HALT,
  input  CLK,
  input  RESET,
  output HALTED
);

  wire register_1_q;

  or or_1 (HALTED, EX_HALT, register_1_q);
  Register #(.width(1)) register_1 (.D(HALTED), .en(1'b1), .Q(register_1_q), .clk(CLK), .clr(RESET));
endmodule
